# Fritzing sketch dtmf01 (saved by Fritzing 0.9.1b)
breadboards: 2

parts:
  IC1 = IC, DIP package, 18 pins [chip_label=IC part_number=CM8870]
  XTAL1 = Crystal [frequency="4 MHz" package=SMD]
  C1 = Capacitor [package=cap-pth-small2]
  RJ-1 = RJ-11 Connector with Breakout Board
  RJ-2 = RJ-11 Connector with Breakout Board
  R2 = Resistor [tolerance=±5% resistance=330k package=THT]
  R3 = Resistor [tolerance=±5% resistance=22k package=THT]
  R4 = Resistor [tolerance=±5% resistance=22k package=THT]
  C2 = Ceramic Capacitor [capacitance=100nF package="100 mil [THT, multilayer]"]
  R5 = Resistor [tolerance=±5% resistance=15k package=THT]
  R7 = TRIMPOT [package=trimpot_pth_s3_lock]
  R8 = Resistor [tolerance=±5% resistance=330 package=THT]
  R9 = Resistor [tolerance=±5% resistance=330 package=THT]
  R10 = Resistor [tolerance=±5% resistance=330 package=THT]
  R11 = Resistor [tolerance=±5% resistance=330 package=THT]
  LED1 = Super Flux LED blue [color=Red]
  LED2 = Super Flux LED blue [color=Yellow]
  LED3 = Super Flux LED blue [color=Green]
  LED4 = Super Flux LED blue [color=Blue]
  R12 = Resistor [tolerance=±5% resistance=330 package=THT]
  LED5 = Super Flux LED blue [color=White]

nets:
  N1: IC1.pin1, IC1.pin4
  N2: IC1.pin3, R7.WIPER, R7.CW
  GND: IC1.pin5, IC1.pin6, IC1.pin9, RJ-1.GND, RJ-2.GND, R3.Pin_1, R4.Pin_0, LED1.cathode, LED2.cathode, LED3.cathode, LED4.cathode, LED5.cathode
  N3: IC1.pin7, XTAL1.pin_0
  N4: IC1.pin8, XTAL1.pin_1
  N5: IC1.pin10, IC1.pin18, C1.2
  N6: IC1.pin11, R11.Pin_1
  N7: IC1.pin12, R10.Pin_1
  N8: IC1.pin13, R9.Pin_1
  N9: IC1.pin14, R8.Pin_1
  N10: IC1.pin15, R12.Pin_1
  N11: IC1.pin16, R2.Pin_1
  N12: IC1.pin17, C1.1, R2.Pin_0
  VCC: RJ-1.Vcc, RJ-2.Vcc, R3.Pin_0, R4.Pin_1, C2.1
  N13: C2.0, R5.Pin_1
  N14: R5.Pin_0, R7.CCW
  N15: R8.Pin_0, LED1.anode
  N16: R9.Pin_0, LED2.anode
  N17: R10.Pin_0, LED3.anode
  N18: R11.Pin_0, LED4.anode
  N19: R12.Pin_0, LED5.anode
