# Fritzing sketch dtmf_0 (saved by Fritzing 0.9.1b)
breadboards: 2

parts:
  IC2 = IC, DIP package, 18 pins [chip_label=IC part_number=CM8870]
  R1 = Resistor [tolerance=±5% resistance=100k package="0603 [SMD]"]
  R2 = Resistor [tolerance=±5% resistance=100k package="0603 [SMD]"]
  C1 = Electrolytic Capacitor [capacitance=10µF voltage=50V package="0405 [SMD, electrolytic]"]
  XTAL1 = Crystal [frequency="4 MHz" package=THT]
  C3 = Ceramic Capacitor [capacitance=100nF package="200 mil [THT, multilayer]"]
  R3 = Resistor [tolerance=±5% resistance=330k package="0603 [SMD]"]
  R4 = Resistor [tolerance=±5% resistance=330 package="0603 [SMD]"]
  R5 = Resistor [tolerance=±5% resistance=330 package="0603 [SMD]"]
  R6 = Resistor [tolerance=±5% resistance=330 package="0603 [SMD]"]
  R7 = Resistor [tolerance=±5% resistance=330 package="0603 [SMD]"]
  R8 = Resistor [tolerance=±5% resistance=330 package="0603 [SMD]"]
  LED1 = Super Flux LED blue [color=Green]
  LED2 = Super Flux LED blue [color=Red]
  LED3 = Super Flux LED blue [color=White]
  LED4 = Super Flux LED blue [color=Blue]
  LED5 = Super Flux LED blue [color=Yellow]
  U4 = 2.5mm Audio Jack [package=stereojack2.5mm_stereojack2.5mm]
  Parte1 = Arduino Uno (Rev3)

nets:
  N1: IC2.pin1, IC2.pin4
  N2: IC2.pin2, R1.Pin_0, R2.Pin_1
  N3: IC2.pin3, R1.Pin_1
  N4: IC2.pin5, IC2.pin6, IC2.pin9, LED1.cathode, LED2.cathode, LED3.cathode, LED4.cathode, LED5.cathode, Parte1.GND
  N5: IC2.pin7, XTAL1.pin_1
  N6: IC2.pin8, XTAL1.pin_0
  N7: IC2.pin10, IC2.pin18, C3.0, U4.SLEEVE, Parte1.5V
  N8: IC2.pin11, R8.Pin_1, Parte1.D6_PWM
  N9: IC2.pin12, R7.Pin_1, Parte1.D5_PWM
  N10: IC2.pin13, R6.Pin_1, Parte1.D4
  N11: IC2.pin14, R5.Pin_1, Parte1.D3_PWM
  N12: IC2.pin15, R4.Pin_1, Parte1.D2
  N13: IC2.pin16, R3.Pin_0
  N14: IC2.pin17, C3.1, R3.Pin_1
  N15: R2.Pin_0, C1.-
  N16: C1.+, U4.RIGHT
  N17: R4.Pin_0, LED1.anode
  N18: R5.Pin_0, LED2.anode
  N19: R6.Pin_0, LED3.anode
  N20: R7.Pin_0, LED4.anode
  N21: R8.Pin_0, LED5.anode
