# Fritzing sketch dtmf_1 (saved by Fritzing 0.9.1b)
breadboards: 1

parts:
  Parte1 = Arduino Prototyping Shield
  RJ-1 = RJ-11 Connector with Breakout Board
  TRRS1 = Audio Jack (TRRS) 3.5mm [part_number="LUMBERG JEITA RC-5325A" package="RC-5325A [SMD]"]
  IC1 = IC, DIP package, 18 pins [chip_label=IC]
  RJ-2 = RJ-11 Connector with Breakout Board
  Y1 = CRYSTAL [package=hc49us]
  R1 = Resistor [tolerance=±5% resistance=100k package="0805 [SMD]"]
  R2 = Resistor [tolerance=±5% resistance=100k package="0805 [SMD]"]
  JP1 = Header 1 [package=1x01_offset]
  JP2 = Header 1 [package=1x01_offset]
  JP3 = Header 1 [package=1x01_offset]
  JP4 = Header 1 [package=1x01_offset]
  R3 = Resistor [tolerance=±5% resistance=330 package="0805 [SMD]"]
  R4 = Resistor [tolerance=±5% resistance=330 package="0805 [SMD]"]
  LED1 = Super Flux LED blue [color=Green]
  LED2 = Super Flux LED blue [color=Yellow]
  C1 = Ceramic Capacitor [capacitance=100nF voltage=50V package="0603 [SMD, multilayer]"]
  C2 = Ceramic Capacitor [capacitance=100nF voltage=50V package="0603 [SMD, multilayer]"]
  R5 = Resistor [tolerance=±5% resistance=330k package="0805 [SMD]"]

nets:
  N1: Parte1.D13, R3.Pin_0
  GND: Parte1.GND, Parte1.N$53, Parte1.N$72, Parte1.N$86, Parte1.N$118, Parte1.N$189, Parte1.N$321, RJ-1.GND, TRRS1.RING1, IC1.pin5, IC1.pin6, IC1.pin9, RJ-2.GND, LED1.cathode, LED2.cathode
  N2: Parte1.D2, Parte1.N$65, Parte1.N$434, IC1.pin15, R4.Pin_0
  N3: Parte1.D3, Parte1.N$79, IC1.pin14
  N4: Parte1.D4, Parte1.N$84, IC1.pin13
  N5: Parte1.D5, Parte1.N$87, IC1.pin12
  N6: Parte1.D6, Parte1.N$67, IC1.pin11
  N7: Parte1.+5V, Parte1.N$34, Parte1.N$178, Parte1.N$190, IC1.pin10, IC1.pin18, C2.0
  N8: Parte1.N$27, Parte1.N$28, Parte1.N$61, Parte1.N$62, IC1.pin1, IC1.pin4
  N9: Parte1.N$37, IC1.pin2, R2.Pin_0
  N10: Parte1.N$41, IC1.pin17, C2.1, R5.Pin_0
  N11: Parte1.N$48, IC1.pin3, R1.Pin_0
  N12: Parte1.N$54, Parte1.N$55, IC1.pin16, R5.Pin_1
  N13: Parte1.N$76, Parte1.N$119, IC1.pin8, Y1.1
  N14: Parte1.N$77, Parte1.N$94, IC1.pin7, Y1.2
  N15: Parte1.N$240, R3.Pin_1, LED1.anode
  N16: Parte1.N$276, TRRS1.SLEEVE, JP4.1
  N17: Parte1.N$277, Parte1.N$291, Parte1.N$374, JP1.1, JP3.1, C1.0
  N18: Parte1.N$289, Parte1.N$364, R1.Pin_1, R2.Pin_1, C1.1
  N19: Parte1.N$292, Parte1.N$322, Parte1.N$404, RJ-1.PRB, RJ-2.PRB, JP2.1
  N20: Parte1.N$304, Parte1.N$305, Parte1.N$311, R4.Pin_1, LED2.anode
  N21: Parte1.N$324, RJ-2.Vcc
  N22: Parte1.N$401, RJ-1.Vcc

notes:
  Nota: todas las conexiones van por la parte inferior
